// Logisim project uart-decoding-logic.circ as structural Verilog: 1 circuit, main circuit main
module main (
  input  Rx,
  input  Clear,
  output out_3,
  output out_4,
  output out_5,
  output out_6,
  output out_7,
  output out_8
);

  wire and_1_out, and_2_out, clock_1_out, not_1_out, not_2_out, shift_register_1_q6, shift_register_1_q7;

  Clock clock_1 (.out(clock_1_out));
  and and_1 (and_1_out, clock_1_out, not_2_out);
  Shift_Register shift_register_1 (
    .in(Rx), .clk(and_1_out), .clr(Clear), .q0(out_3), .q1(out_4), .q2(out_5), .q3(out_6), .q4(out_7),
    .q5(out_8), .q6(shift_register_1_q6), .q7(shift_register_1_q7));  // open: shift, out, load, d0, d1, d2, d3, d4, d5, d6, d7
  not not_1 (not_1_out, shift_register_1_q6);
  and and_2 (and_2_out, shift_register_1_q7, not_1_out);
  not not_2 (not_2_out, and_2_out);
endmodule
